// Logisim project 11)a.circ as structural Verilog
module _14 (
  input  A,
  input  B,
  input  C,
  input  D,
  output F
);

  wire and_1_out, and_2_out, not_1_out;

  and and_1 (and_1_out, A, B);
  not not_1 (not_1_out, C);
  or or_1 (F, not_1_out, and_2_out);
  and and_2 (and_2_out, and_1_out, D);
endmodule

module _11a (
  input  A,
  input  B,
  input  C,
  input  D,
  output F
);

  wire and_1_out, and_2_out, and_3_out, and_4_out, not_1_out, not_2_out;

  not not_1 (not_1_out, A);
  and and_1 (and_1_out, not_1_out, B);
  not not_2 (not_2_out, D);
  and and_2 (and_2_out, B, C);
  and and_3 (and_3_out, and_1_out, not_2_out);
  and and_4 (and_4_out, and_2_out, D);
  or or_1 (F, and_3_out, and_4_out);
endmodule
