// Logisim project TP3.1.circ as structural Verilog
module TP3_1 (
  input  S,
  input  R,
  output Q,
  output Q2
);

  and and_1 (Q, S, R);
  not not_1 (Q2, R);
endmodule
