// Logisim project TP3.3.circ as structural Verilog: 1 circuit, main circuit main
module main (
  input  X,
  output Y
);

  wire and_1_out, d_ff_1_q, d_ff_2_q, d_ff_2_qn, not_1_out, not_2_out, not_3_out, or_1_out;

  not not_1 (not_1_out, X);
  buf or_1 (or_1_out, not_2_out);  // OR_Gate
  not not_2 (not_2_out, d_ff_2_qn);
  and and_1 (and_1_out, X, d_ff_1_q);
  not not_3 (not_3_out, X);
  D_Flip_Flop d_ff_1 (.clk(X), .D(or_1_out), .Q(d_ff_1_q));  // open: Qn, preset, en, reset
  D_Flip_Flop d_ff_2 (.D(not_3_out), .Q(d_ff_2_q), .Qn(d_ff_2_qn));  // open: clk, preset, en, reset
  and and_2 (Y, d_ff_2_q, not_3_out, d_ff_1_q);
endmodule
