// Logisim project ejercicio 4 combinacionales.circ as structural Verilog: 1 circuit, main circuit main
module main (
  input  A,
  input  B,
  input  C,
  output F
);

  wire and_1_out, and_2_out, and_3_out, not_1_out, not_2_out;

  not not_1 (not_1_out, C);
  not not_2 (not_2_out, A);
  and and_1 (and_1_out, A, B, not_1_out);
  and and_2 (and_2_out, B, not_1_out);
  and and_3 (and_3_out, not_2_out, B);
  or or_1 (F, and_1_out, and_2_out, and_3_out);

  // Notes on the sheet:
  //   ABC´+BC´+A´B
endmodule
