// Logisim project Circuitos logicos.circ as structural Verilog
module Ej_1 (
);

  wire and_1_out, or_1_out, undriven, undriven_2, undriven_3, undriven_4;

  and and_1 (and_1_out, undriven, undriven_2);
  or or_1 (or_1_out, undriven_3, undriven_4);

  // Notes on the sheet:
  //   1)
  //   101100111000
  //   000111001101
  //   101100111000
  //   000111001101
  //   000100001000
  //   101111111101
endmodule

module Ej2 (
  input  A,
  input  A_2,
  input  B,
  input  B_2,
  input  C,
  input  C_2,
  input  B_3,
  input  A_3,
  input  B_4,
  input  C_3,
  input  C_4,
  input  A_4
);

  wire and_1_out, and_2_out, and_3_out, and_4_out, nor_1_out, not_1_out, or_1_out, or_2_out, or_3_out;

  not not_1 (not_1_out, A_3);
  or or_1 (or_1_out, A, B);
  or or_2 (or_2_out, or_1_out, C);
  or or_3 (or_3_out, not_1_out, B_4);
  and and_1 (and_1_out, or_3_out, C_4);
  and and_2 (and_2_out, A_2, B_2);
  nor nor_1 (nor_1_out, B_3, C_3);
  and and_3 (and_3_out, and_2_out, C_2);
  and and_4 (and_4_out, nor_1_out, A_4);

  // Notes on the sheet:
  //   2)
  //   A= 1100110110
  //   A) (A+B+C)
  //   C) (C*(A'+B)
  //   B=1110000111
  //   (A+B+C)
  //   C=1010010110
  //   (C*(A'+B)
  //   B) (A*B*C)
  //   D) (B+C)'*A
  //   (A*B*C)
  //   (B+C)'*A
endmodule

module Ej3 (
);

  wire or_1_out;

  // OR_Gate or_1 has open pins: out=or_1_out

  // Notes on the sheet:
  //   3)
  //   A)
  //   A)
endmodule
